// Logisim project 16 bit MicroP - FINAL.circ as structural Verilog: 4 circuits, main circuit main
module ALU (
  input  [15:0] Input_A,
  input  [15:0] Input_B,
  input  [1:0] Select_Input,
  output [15:0] Output
);

  wire [15:0] adder_1_out, and_1_out, or_1_out, subtractor_1_out;

  Adder #(.width(16)) adder_1 (.a(Input_A), .b(Input_B), .out(adder_1_out));  // open: cin, cout
  Subtractor #(.width(16)) subtractor_1 (.a(Input_A), .b(Input_B), .out(subtractor_1_out));  // open: bin, bout
  assign and_1_out = Input_A & Input_B;  // AND_Gate and_1, 16 bits wide
  assign or_1_out = Input_A | Input_B;  // OR_Gate or_1, 16 bits wide
  Multiplexer #(.select(2), .width(16), .enable("false")) multiplexer_1 (
    .in0(adder_1_out), .in1(subtractor_1_out), .in2(and_1_out), .in3(or_1_out), .out(Output),
    .sel(Select_Input));
endmodule

// 1
module main (
  input  Clear_RAM,
  input  Clear_Register_File
);

  wire and_1_out, clock_1_out, comparator_1_eq, comparator_2_eq, control_unit_1_branchenable,
       control_unit_1_jumpenable, control_unit_1_loadenable, control_unit_1_mux1, control_unit_1_mux2,
       control_unit_1_mux3, control_unit_1_mux4, control_unit_1_regwrite, control_unit_1_storeenable,
       multiplexer_3_out, not_1_out, or_1_out;
  wire [1:0] control_unit_1_alus0;
  wire [3:0] multiplexer_2_out;
  wire [15:0] adder_1_out, adder_2_out, ALU_output, bit_extender_1_out, multiplexer_1_out, multiplexer_4_out,
       multiplexer_5_out, PC_q, ram_1_data, Register_File_read_data_1, Register_File_read_data_2,
       Register_File_read_data_3, rom_1_data;

  Clock clock_1 (.out(clock_1_out));
  Multiplexer #(.width(16), .enable("false")) multiplexer_1 (
    .in0(adder_2_out), .in1(adder_1_out), .out(multiplexer_1_out), .sel(or_1_out));
  Register #(.width(16)) PC (.D(multiplexer_1_out), .Q(PC_q), .clk(clock_1_out));  // open: en, clr
  Adder #(.width(16)) adder_1 (.a(Register_File_read_data_3), .b(PC_q), .out(adder_1_out));  // open: cin, cout
  Adder #(.width(16)) adder_2 (.a(PC_q), .b(16'h1), .out(adder_2_out));  // open: cin, cout
  or or_1 (or_1_out, and_1_out, control_unit_1_jumpenable);
  ROM #(.addrWidth(16), .dataWidth(16)) rom_1 (.addr(PC_q), .data(rom_1_data), .sel(1'b1));
  and and_1 (and_1_out, multiplexer_3_out, control_unit_1_branchenable);
  Comparator #(.width(16)) comparator_1 (
    .a(Register_File_read_data_1), .b(Register_File_read_data_2), .eq(comparator_1_eq));  // open: gt, lt
  Comparator #(.width(16)) comparator_2 (
    .a(Register_File_read_data_1), .b(Register_File_read_data_2), .eq(comparator_2_eq));  // open: gt, lt
  Multiplexer #(.width(4), .enable("false")) multiplexer_2 (
    .in0(rom_1_data[3:0]), .in1(rom_1_data[11:8]), .out(multiplexer_2_out), .sel(control_unit_1_mux2));
  Control_Unit control_unit_1 (
    .B15(rom_1_data[15]), .ALUS1(control_unit_1_alus0[1]), .B14(rom_1_data[14]), .B13(rom_1_data[13]),
    .ALUS0(control_unit_1_alus0[0]), .B12(rom_1_data[12]), .RegWrite(control_unit_1_regwrite),
    .MUX1(control_unit_1_mux1), .MUX2(control_unit_1_mux2), .MUX3(control_unit_1_mux3),
    .LoadEnable(control_unit_1_loadenable), .StoreEnable(control_unit_1_storeenable),
    .MUX4(control_unit_1_mux4), .JumpEnable(control_unit_1_jumpenable),
    .BranchEnable(control_unit_1_branchenable));
  not not_1 (not_1_out, comparator_2_eq);
  Multiplexer #(.enable("false")) multiplexer_3 (
    .in0(comparator_1_eq), .in1(not_1_out), .out(multiplexer_3_out), .sel(control_unit_1_mux4));
  assign bit_extender_1_out = {{12{rom_1_data[7]}}, rom_1_data[7:4]};  // Bit_Extender bit_extender_1
  _16_bit_Register_File Register_File (
    .Read_Address_1(rom_1_data[11:8]), .Read_Address_2(rom_1_data[7:4]), .Write_Address(multiplexer_2_out),
    .Write_Data(multiplexer_5_out), .Read_Data_1(Register_File_read_data_1),
    .Read_Data_2(Register_File_read_data_2), .regWrite(control_unit_1_regwrite), .Clock(clock_1_out),
    .Read_Data_3(Register_File_read_data_3), .Read_Address_3(rom_1_data[3:0]), .Clear(Clear_Register_File));
  Multiplexer #(.width(16), .enable("false")) multiplexer_4 (
    .in0(Register_File_read_data_2), .in1(bit_extender_1_out), .out(multiplexer_4_out),
    .sel(control_unit_1_mux1));
  Multiplexer #(.width(16), .enable("false")) multiplexer_5 (
    .in0(ALU_output), .in1(ram_1_data), .out(multiplexer_5_out), .sel(control_unit_1_mux3));
  RAM #(.addrWidth(16), .dataWidth(16), .bus("separate")) ram_1 (
    .addr(Register_File_read_data_1), .din(Register_File_read_data_2), .data(ram_1_data),
    .str(control_unit_1_storeenable), .sel(1'b1), .clk(clock_1_out), .ld(control_unit_1_loadenable),
    .clr(Clear_RAM));
  ALU ALU (
    .Output(ALU_output), .Input_A(Register_File_read_data_1), .Input_B(multiplexer_4_out),
    .Select_Input(control_unit_1_alus0));

  // Notes on the sheet:
  //   BranchEnable
  //   contents of rom_1 (hex, n*v repeats v):
  //   a123 8123 6231 4*0 8123 7123
  //   MUX2
  //   MUX4
  //   RAM
  //   MUX1
  //   MUX3
endmodule

module _16_bit_Register_File (
  input  [3:0] Read_Address_1,
  input  [3:0] Read_Address_2,
  input  [3:0] Read_Address_3,
  input  [3:0] Write_Address,
  input  [15:0] Write_Data,
  input  regWrite,
  input  Clock,
  input  Clear,
  output [15:0] Read_Data_1,
  output [15:0] Read_Data_2,
  output [15:0] Read_Data_3
);

  wire and_1_out, and_2_out, and_3_out, and_4_out, and_5_out, and_6_out, and_7_out, and_8_out, and_9_out,
       and_10_out, and_11_out, and_12_out, and_13_out, and_14_out, and_15_out, and_16_out, decoder_1_out0,
       decoder_1_out1, decoder_1_out2, decoder_1_out3, decoder_1_out4, decoder_1_out5, decoder_1_out6,
       decoder_1_out7, decoder_1_out8, decoder_1_out9, decoder_1_out10, decoder_1_out11, decoder_1_out12,
       decoder_1_out13, decoder_1_out14, decoder_1_out15;
  wire [15:0] register_1_q, register_2_q, register_3_q, register_4_q, register_5_q, register_6_q,
       register_7_q, register_8_q, register_9_q, register_10_q, register_11_q, register_12_q, register_13_q,
       register_14_q, register_15_q, register_16_q;

  Decoder #(.select(4)) decoder_1 (
    .out0(decoder_1_out0), .out1(decoder_1_out1), .out2(decoder_1_out2), .out3(decoder_1_out3),
    .out4(decoder_1_out4), .out5(decoder_1_out5), .out6(decoder_1_out6), .out7(decoder_1_out7),
    .out8(decoder_1_out8), .out9(decoder_1_out9), .out10(decoder_1_out10), .out11(decoder_1_out11),
    .out12(decoder_1_out12), .out13(decoder_1_out13), .out14(decoder_1_out14), .out15(decoder_1_out15),
    .sel(Write_Address));  // open: en
  and and_1 (and_1_out, decoder_1_out0, regWrite);
  and and_2 (and_2_out, decoder_1_out1, regWrite);
  and and_3 (and_3_out, decoder_1_out2, regWrite);
  and and_4 (and_4_out, decoder_1_out3, regWrite);
  and and_5 (and_5_out, decoder_1_out4, regWrite);
  and and_6 (and_6_out, decoder_1_out5, regWrite);
  and and_7 (and_7_out, decoder_1_out6, regWrite);
  and and_8 (and_8_out, decoder_1_out7, regWrite);
  Register #(.width(16)) register_1 (.D(Write_Data), .en(and_1_out), .Q(register_1_q), .clk(Clock), .clr(Clear));
  Register #(.width(16)) register_2 (.D(Write_Data), .en(and_2_out), .Q(register_2_q), .clk(Clock), .clr(Clear));
  Register #(.width(16)) register_3 (.D(Write_Data), .en(and_3_out), .Q(register_3_q), .clk(Clock), .clr(Clear));
  Register #(.width(16)) register_4 (.D(Write_Data), .en(and_4_out), .Q(register_4_q), .clk(Clock), .clr(Clear));
  Register #(.width(16)) register_5 (.D(Write_Data), .en(and_5_out), .Q(register_5_q), .clk(Clock), .clr(Clear));
  Register #(.width(16)) register_6 (.D(Write_Data), .en(and_6_out), .Q(register_6_q), .clk(Clock), .clr(Clear));
  Register #(.width(16)) register_7 (.D(Write_Data), .en(and_7_out), .Q(register_7_q), .clk(Clock), .clr(Clear));
  Register #(.width(16)) register_8 (.D(Write_Data), .en(and_8_out), .Q(register_8_q), .clk(Clock), .clr(Clear));
  and and_9 (and_9_out, decoder_1_out8, regWrite);
  and and_10 (and_10_out, decoder_1_out9, regWrite);
  and and_11 (and_11_out, decoder_1_out10, regWrite);
  and and_12 (and_12_out, decoder_1_out11, regWrite);
  and and_13 (and_13_out, decoder_1_out12, regWrite);
  and and_14 (and_14_out, decoder_1_out13, regWrite);
  and and_15 (and_15_out, decoder_1_out14, regWrite);
  and and_16 (and_16_out, decoder_1_out15, regWrite);
  Register #(.width(16)) register_9 (.D(Write_Data), .en(and_9_out), .Q(register_9_q), .clk(Clock), .clr(Clear));
  Register #(.width(16)) register_10 (.D(Write_Data), .en(and_10_out), .Q(register_10_q), .clk(Clock), .clr(Clear));
  Register #(.width(16)) register_11 (.D(Write_Data), .en(and_11_out), .Q(register_11_q), .clk(Clock), .clr(Clear));
  Register #(.width(16)) register_12 (.D(Write_Data), .en(and_12_out), .Q(register_12_q), .clk(Clock), .clr(Clear));
  Register #(.width(16)) register_13 (.D(Write_Data), .en(and_13_out), .Q(register_13_q), .clk(Clock), .clr(Clear));
  Register #(.width(16)) register_14 (.D(Write_Data), .en(and_14_out), .Q(register_14_q), .clk(Clock), .clr(Clear));
  Register #(.width(16)) register_15 (.D(Write_Data), .en(and_15_out), .Q(register_15_q), .clk(Clock), .clr(Clear));
  Register #(.width(16)) register_16 (.D(Write_Data), .en(and_16_out), .Q(register_16_q), .clk(Clock), .clr(Clear));
  Multiplexer #(.select(4), .width(16), .enable("false")) multiplexer_1 (
    .in0(register_1_q), .in1(register_2_q), .in2(register_3_q), .in3(register_4_q), .in4(register_5_q),
    .in5(register_6_q), .in6(register_7_q), .in7(register_8_q), .in8(register_9_q), .in9(register_10_q),
    .in10(register_11_q), .in11(register_12_q), .in12(register_13_q), .in13(register_14_q),
    .in14(register_15_q), .in15(register_16_q), .out(Read_Data_1), .sel(Read_Address_1));
  Multiplexer #(.select(4), .width(16), .enable("false")) multiplexer_2 (
    .in0(register_1_q), .in1(register_2_q), .in2(register_3_q), .in3(register_4_q), .in4(register_5_q),
    .in5(register_6_q), .in6(register_7_q), .in7(register_8_q), .in8(register_9_q), .in9(register_10_q),
    .in10(register_11_q), .in11(register_12_q), .in12(register_13_q), .in13(register_14_q),
    .in14(register_15_q), .in15(register_16_q), .out(Read_Data_2), .sel(Read_Address_2));
  Multiplexer #(.select(4), .width(16), .enable("false")) multiplexer_3 (
    .in0(register_1_q), .in1(register_2_q), .in2(register_3_q), .in3(register_4_q), .in4(register_5_q),
    .in5(register_6_q), .in6(register_7_q), .in7(register_8_q), .in8(register_9_q), .in9(register_10_q),
    .in10(register_11_q), .in11(register_12_q), .in12(register_13_q), .in13(register_14_q),
    .in14(register_15_q), .in15(register_16_q), .out(Read_Data_3), .sel(Read_Address_3));
endmodule

module Control_Unit (
  input  B15,
  input  B14,
  input  B13,
  input  B12,
  output ALUS1,
  output ALUS0,
  output RegWrite,
  output MUX1,
  output MUX2,
  output MUX3,
  output LoadEnable,
  output StoreEnable,
  output MUX4,
  output JumpEnable,
  output BranchEnable
);

  wire and_1_out, and_2_out, and_3_out, and_4_out, and_5_out, and_6_out, and_7_out, not_1_out, not_2_out,
       not_3_out, not_4_out, not_5_out, not_6_out, not_7_out, not_8_out, not_9_out, not_10_out, not_11_out,
       not_12_out, not_13_out, not_14_out, not_15_out;

  and and_1 (and_1_out, B14, B12);
  not not_1 (not_1_out, B14);
  and and_2 (and_2_out, not_1_out, B12);
  and and_3 (and_3_out, B14, B13);
  not not_2 (not_2_out, B15);
  and and_4 (and_4_out, not_2_out, not_3_out);
  not not_3 (not_3_out, B14);
  not not_4 (not_4_out, B15);
  and and_5 (and_5_out, not_4_out, not_5_out);
  not not_5 (not_5_out, B13);
  not not_6 (not_6_out, B14);
  and and_6 (and_6_out, not_6_out, not_7_out, B12);
  not not_7 (not_7_out, B13);
  or or_1 (MUX1, B14, B15);
  and and_7 (and_7_out, B14, B13);
  not not_8 (not_8_out, B14);
  not not_9 (not_9_out, B13);
  not not_10 (not_10_out, B14);
  not not_11 (not_11_out, B12);
  not not_12 (not_12_out, B14);
  not not_13 (not_13_out, B13);
  not not_14 (not_14_out, B12);
  not not_15 (not_15_out, B15);
  and and_8 (BranchEnable, not_15_out, B14, B13);
  or or_2 (ALUS1, B13, and_1_out, B15);
  or or_3 (ALUS0, and_2_out, and_3_out, B15);
  or or_4 (RegWrite, and_4_out, and_5_out, and_6_out);
  or or_5 (MUX3, and_7_out, B15);
  and and_9 (LoadEnable, B15, not_8_out, not_9_out, B12);
  and and_10 (StoreEnable, B15, not_10_out, B13, not_11_out);
  and and_11 (JumpEnable, B15, not_12_out, not_13_out, not_14_out);

  assign MUX2 = B15;
  assign MUX4 = B12;
endmodule
